# Fritzing sketch diagram_tork_throttle (saved by Fritzing 0.9.10b)
circuit board: 8.46667cm x 5.64444cm
perfboards: 1

parts:
  R1 = Resistor [tolerance=±1% power=0.25 resistance=1k package=THT]
  C1 = Electrolytic Capacitor [capacitance=0.1µF voltage=35V package="100 mil [THT, electrolytic]"]
  J4 = male pin header, 3 pins [form="♂ (male)"]
  J3 = male pin header, 2 pins [form="♂ (male)"]
  J5 = male pin header, 2 pins [form="♂ (male)"]
  J6 = male alternating pin header, 3 pins [form="♂ (male)"]
  Composant1 = Arduino Nano (Rev3.0)
  J7 = male pin header, 2 pins [form="♂ (male)"]

nets:
  N1: R1.Pin_0, Composant1.D3
  N2: R1.Pin_1, C1.+, J3.pin1
  GND: C1.-, J4.pin2, J3.pin2, J5.pin2, J6.pin2, Composant1.GND
  N3: J4.pin1, Composant1.D2
  5V: J4.pin3
  N4: J5.pin1, Composant1.VIN
  N5: J6.pin3, Composant1.A1
  N6: Composant1.D4, J7.pin2

notes:
  + Vin (7V-12V)
  Common GND
  +5V
  signal out (PWM D3)
  Gnd
  signal in (D2 interupt !)
  PAS In (from torque)
  LED BUILTIN (D13)
  +
  S (D10)
  S (D2)
  RC filter
  not mandatory
  (with controler)
  Torque to throttle, Chris74
  signal in (A1)
  Torque signal
  Vin 7-12V
  Gnd commun
  S (A1)
  Throttle Out
  PAS Out
  signal out (D4)
